# Fritzing sketch rpi_simpleled (saved by Fritzing 0.7.12b)
breadboards: 1

parts:
  Raspberry_Pi1 = Raspberry Pi (Model B)
  LED1 = LED - 5mm [color="Red (633nm)" package="5 mm [THT]"]
  R1 = Resistor [tolerance=±5% resistance=220 package=THT]

nets:
  N1: Raspberry_Pi1.GND, LED1.cathode
  N2: Raspberry_Pi1.#4, R1.Pin_1
  N3: LED1.anode, R1.Pin_0

custom parts:
  Raspberry Pi (Model B): Raspberry Pi Single-board Computer, Model B
