# Fritzing sketch rsp_24c04 (saved by Fritzing 0.7.12b)
breadboards: 1

parts:
  Raspberry_Pi1 = Raspberry Pi (Model B)
  IC1 = 24LC02 [package=THT]

nets:
  N1: Raspberry_Pi1.3V3, IC1.+V
  N2: Raspberry_Pi1.SDA, IC1.SDA_-_I2C_Data
  N3: Raspberry_Pi1.SCL, IC1.SCL_-_I2C_Clock
  N4: Raspberry_Pi1.GND, IC1.A0, IC1.A1, IC1.A2, IC1.0V

custom parts:
  Raspberry Pi (Model B): Raspberry Pi Single-board Computer, Model B
